// Logisim project add4 com tabela.circ as structural Verilog: 3 circuits, main circuit main
module main (
  input  [3:0] in_1,
  input  [3:0] in_2,
  output Overflow,
  output [3:0] out_4
);

  // Probe on in_1
  // Probe on in_2
  ADD_4 add_4_1 (.Overflow(Overflow), .in_1(in_1), .in_2(in_2), .out_4(out_4));
  // Probe on out_4
endmodule

module ADD_1 (
  input  A,
  input  B,
  input  C,
  output S,
  output V
);

  wire and_1_out, and_2_out, and_3_out, and_4_out, and_5_out, and_6_out, and_7_out;

  and and_1 (and_1_out, ~A, ~B, C);  // AND_Gate
  and and_2 (and_2_out, ~A, B, ~C);  // AND_Gate
  and and_3 (and_3_out, A, ~B, ~C);  // AND_Gate
  and and_4 (and_4_out, A, B, C);
  and and_5 (and_5_out, ~A, B, C);  // AND_Gate
  and and_6 (and_6_out, A, ~B, C);  // AND_Gate
  and and_7 (and_7_out, A, B, ~C);  // AND_Gate
  or or_1 (S, and_1_out, and_2_out, and_3_out, and_4_out);
  or or_2 (V, and_5_out, and_6_out, and_7_out, and_4_out);
endmodule

module ADD_4 (
  input  [3:0] in_1,
  input  [3:0] in_2,
  output Overflow,
  output [3:0] out_4
);

  wire add_1_2_v, add_1_3_v, add_1_4_v;

  ADD_1 add_1_1 (.S(out_4[3]), .V(Overflow), .A(in_2[3]), .B(in_1[3]), .C(add_1_2_v));
  ADD_1 add_1_2 (.S(out_4[2]), .V(add_1_2_v), .A(in_2[2]), .B(in_1[2]), .C(add_1_3_v));
  ADD_1 add_1_3 (.S(out_4[1]), .V(add_1_3_v), .A(in_2[1]), .B(in_1[1]), .C(add_1_4_v));
  ADD_1 add_1_4 (.S(out_4[0]), .V(add_1_4_v), .A(in_2[0]), .B(in_1[0]), .C(1'b0));
endmodule
