// Logisim project eu desisto.circ as structural Verilog
module coisa_que_liga_no_display (
  input  A,
  input  B,
  input  C,
  input  D,
  output A_2,
  output B_2,
  output C_2,
  output D_2,
  output E,
  output F,
  output G
);

  wire and_1_out, and_2_out, and_3_out, and_4_out, and_5_out, and_6_out, and_7_out, or_1_out, or_2_out,
       or_3_out, or_4_out, or_5_out, or_6_out, or_7_out, xor_1_out, xor_2_out;

  and and_1 (and_1_out, ~A, ~A);  // AND_Gate
  xor xor_1 (xor_1_out, A, A);
  and and_2 (and_2_out, ~A, A);  // AND_Gate
  xor xor_2 (xor_2_out, A, A);
  and and_3 (and_3_out, A, A, A);
  and and_4 (and_4_out, A, ~A, ~A);  // AND_Gate
  and and_5 (and_5_out, ~A, ~A, A);  // AND_Gate
  or or_1 (or_1_out, A, ~A);  // OR_Gate
  or or_2 (or_2_out, ~A, ~A);  // OR_Gate
  or or_3 (or_3_out, A, A);
  or or_4 (or_4_out, A, ~A);  // OR_Gate
  or or_5 (or_5_out, A, ~A);  // OR_Gate
  and and_6 (and_6_out, ~A, ~A);  // AND_Gate
  and and_7 (and_7_out, A, A, A);
  nand nand_1 (A_2, and_1_out, xor_1_out);
  nand nand_2 (B_2, and_2_out, xor_2_out);
  nand nand_3 (C_2, ~A, ~A, A, ~A);  // NAND_Gate
  or or_6 (or_6_out, and_3_out, and_4_out, and_5_out);
  and and_8 (E, ~A, or_1_out, or_2_out);  // AND_Gate
  or or_7 (or_7_out, and_6_out, and_7_out);
  nand nand_4 (D_2, or_6_out, ~A);  // NAND_Gate
  nand nand_5 (G, or_7_out, ~A);  // NAND_Gate
  nand nand_6 (F, ~A, or_3_out, or_4_out, or_5_out);  // NAND_Gate

  assign B = A;
  assign C = A;
  assign D = A;
endmodule
